// Logisim project cpu-circuit.circ as structural Verilog: 1 circuit, main circuit main
module main (
  input  in_1,
  input  in_2
);

  wire and_1_out, and_2_out, and_4_out, and_5_out, and_6_out, CARR_BIT, CARRY_FLAG, CLK, clock_1_out,
       controlled_buffer_12_out, controlled_buffer_13_out, COUNT_ENABLE, counter_2_carry, d_ff_1_q,
       DISP_REG_WRITE, EI, EO, FLAG_REG_WRITE, INV_CLK, JUMP, LOAD_ROM, MEM_READ, MEM_WRITE,
       n7_segment_display_1_p1, n7_segment_display_2_p1, n7_segment_display_3_p1, n7_segment_display_4_p1,
       n7_segment_display_5_p1, n7_segment_display_6_p1, n7_segment_display_7_p1, n7_segment_display_8_p1,
       n7_segment_display_9_p1, n7_segment_display_10_p1, n7_segment_display_11_p1, n7_segment_display_12_p1,
       not_1_out, not_3_out, not_4_out, not_5_out, not_6_out, not_7_out, not_8_out, not_10_out, not_11_out,
       not_12_out, PRG_CNT_READ, REG_A_READ, REG_A_WRITE, REG_B_WRITE, REG_INS_READ, REG_INS_WRITE,
       REG_MEMADDR_WRITE, ROM_LOAD_CLOCK, STOP, SUB, undriven, ZERO_FLAG;
  wire [1:0] controlled_buffer_16_out;
  wire [3:0] buffer_10_out, controlled_buffer_15_out, controlled_buffer_17_out, INS_DECODER,
       INSTR_STEP_COUNTER_q;
  wire [5:0] rgb_video_1_p3, rgb_video_1_p4;
  wire [7:0] and_3_out, binary_to_bcd_converter_2_p1, buffer_2_out, counter_1_q;
  wire [7:2] register_1_q;
  wire [9:0] dipswitch_2_sw10;
  wire [11:0] controlled_buffer_10_out, counter_4_q, INSTR_REG_q;
  wire [15:0] ALU_IN_A, ALU_IN_B, ALU_VALUE, buffer_3_out, BUS_1, controlled_buffer_19_out,
       controlled_inverter_1_out, dipswitch_1_sw16, DISP_REG_q, MEM_ADDRESS_REG_q, MEMORY_dout,
       PROGRAM_ROM_data;

  Clock clock_1 (.out(clock_1_out));
  and and_1 (and_1_out, not_1_out, not_3_out);
  not not_1 (not_1_out, STOP);
  assign ROM_LOAD_CLOCK = LOAD_ROM ? clock_1_out : 1'bz;  // Controlled_Buffer controlled_buffer_1
  assign CLK = LOAD_ROM ? in_1 : 1'bz;  // Controlled_Buffer controlled_buffer_2
  assign CLK = and_1_out ? clock_1_out : 1'bz;  // Controlled_Buffer controlled_buffer_3
  not not_2 (INV_CLK, CLK);
  not not_3 (not_3_out, LOAD_ROM);
  // _7_Segment_Display 7_segment_display_1: pin names not known; wires that end beside it: n7_segment_display_1_p1, n7_segment_display_1_p1
  // BCD_to_7_Segment_decoder bcd_to_7_segment_decoder_1: pin names not known
  // Binary_to_BCD_converter #(.binvalue(8)) binary_to_bcd_converter_1: pin names not known
  // _7_Segment_Display 7_segment_display_2: pin names not known; wires that end beside it: n7_segment_display_2_p1, n7_segment_display_2_p1
  // BCD_to_7_Segment_decoder bcd_to_7_segment_decoder_2: pin names not known
  // _7_Segment_Display 7_segment_display_3: pin names not known; wires that end beside it: n7_segment_display_3_p1, n7_segment_display_3_p1
  // BCD_to_7_Segment_decoder bcd_to_7_segment_decoder_3: pin names not known
  // Buffer buffer_1 is placed but not wired
  LED led_1 (.in(binary_to_bcd_converter_2_p1[7]));
  LED led_2 (.in(binary_to_bcd_converter_2_p1[6]));
  LED led_3 (.in(binary_to_bcd_converter_2_p1[5]));
  LED led_4 (.in(binary_to_bcd_converter_2_p1[4]));
  // _7_Segment_Display 7_segment_display_4: pin names not known; wires that end beside it: n7_segment_display_4_p1, n7_segment_display_4_p1
  // _7_Segment_Display 7_segment_display_5: pin names not known; wires that end beside it: n7_segment_display_5_p1, n7_segment_display_5_p1
  // BCD_to_7_Segment_decoder bcd_to_7_segment_decoder_4: pin names not known
  // BCD_to_7_Segment_decoder bcd_to_7_segment_decoder_5: pin names not known
  // Binary_to_BCD_converter #(.binvalue(8)) binary_to_bcd_converter_2: pin names not known; wires that end beside it: binary_to_bcd_converter_2_p1
  LED led_5 (.in(binary_to_bcd_converter_2_p1[3]));
  LED led_6 (.in(binary_to_bcd_converter_2_p1[2]));
  LED led_7 (.in(binary_to_bcd_converter_2_p1[1]));
  LED led_8 (.in(binary_to_bcd_converter_2_p1[0]));
  // _7_Segment_Display 7_segment_display_6: pin names not known; wires that end beside it: n7_segment_display_6_p1, n7_segment_display_6_p1
  // BCD_to_7_Segment_decoder bcd_to_7_segment_decoder_6: pin names not known
  DipSwitch #(.number(16)) dipswitch_1 (
    .sw1(dipswitch_1_sw16[15]), .sw2(dipswitch_1_sw16[14]), .sw3(dipswitch_1_sw16[13]),
    .sw4(dipswitch_1_sw16[12]), .sw5(dipswitch_1_sw16[11]), .sw6(dipswitch_1_sw16[10]),
    .sw7(dipswitch_1_sw16[9]), .sw8(dipswitch_1_sw16[8]), .sw9(dipswitch_1_sw16[7]),
    .sw10(dipswitch_1_sw16[6]), .sw11(dipswitch_1_sw16[5]), .sw12(dipswitch_1_sw16[4]),
    .sw13(dipswitch_1_sw16[3]), .sw14(dipswitch_1_sw16[2]), .sw15(dipswitch_1_sw16[1]),
    .sw16(dipswitch_1_sw16[0]));
  // Probe on dipswitch_1_sw16
  // XOR_Gate xor_1 has open pins: in0=undriven, out=open
  // XOR_Gate xor_2 has open pins: in0=undriven, out=open
  // XOR_Gate xor_3 has open pins: in0=undriven, out=open
  // XOR_Gate xor_4 has open pins: in0=undriven, out=open
  // XOR_Gate xor_5 has open pins: in0=undriven, out=open
  // XOR_Gate xor_6 has open pins: in0=undriven, out=open
  // XOR_Gate xor_7 has open pins: in0=undriven, out=open
  // XOR_Gate xor_8 has open pins: in0=undriven, out=open
  // _7_Segment_Display 7_segment_display_7: pin names not known; wires that end beside it: n7_segment_display_7_p1, n7_segment_display_7_p1
  // BCD_to_7_Segment_decoder bcd_to_7_segment_decoder_7: pin names not known
  // Binary_to_BCD_converter #(.binvalue(8)) binary_to_bcd_converter_3: pin names not known; wires that end beside it: dipswitch_1_sw16[15:8]
  Register #(.width(16)) A_Reg (.D(BUS_1), .en(REG_A_WRITE), .clk(CLK), .Q(ALU_IN_A));  // open: clr
  // _7_Segment_Display 7_segment_display_8: pin names not known; wires that end beside it: n7_segment_display_8_p1, n7_segment_display_8_p1
  // _7_Segment_Display 7_segment_display_9: pin names not known; wires that end beside it: n7_segment_display_9_p1, n7_segment_display_9_p1
  // BCD_to_7_Segment_decoder bcd_to_7_segment_decoder_8: pin names not known
  // BCD_to_7_Segment_decoder bcd_to_7_segment_decoder_9: pin names not known
  not not_4 (not_4_out, REG_A_WRITE);
  and and_2 (and_2_out, not_4_out, REG_A_READ);
  assign BUS_1 = and_2_out ? ALU_IN_A : 16'bz;  // Controlled_Buffer controlled_buffer_4
  // Probe on ALU_IN_A
  Counter counter_1 (
    .load(JUMP), .count(COUNT_ENABLE), .clk(CLK), .D(BUS_1[7:0]), .Q(counter_1_q));  // open: clr, up, carry
  // _7_Segment_Display 7_segment_display_10: pin names not known; wires that end beside it: n7_segment_display_10_p1, n7_segment_display_10_p1
  // BCD_to_7_Segment_decoder bcd_to_7_segment_decoder_10: pin names not known
  // Binary_to_BCD_converter #(.binvalue(8)) binary_to_bcd_converter_4: pin names not known; wires that end beside it: dipswitch_1_sw16[7:0]
  // _7_Segment_Display 7_segment_display_11: pin names not known; wires that end beside it: n7_segment_display_11_p1, n7_segment_display_11_p1
  // BCD_to_7_Segment_decoder bcd_to_7_segment_decoder_11: pin names not known
  // _7_Segment_Display 7_segment_display_12: pin names not known; wires that end beside it: n7_segment_display_12_p1, n7_segment_display_12_p1
  // BCD_to_7_Segment_decoder bcd_to_7_segment_decoder_12: pin names not known
  assign controlled_inverter_1_out = SUB ? ~ALU_IN_B : 16'bz;  // Controlled_Inverter controlled_inverter_1
  not not_5 (not_5_out, SUB);
  assign controlled_inverter_1_out = not_5_out ? ALU_IN_B : 16'bz;  // Controlled_Buffer controlled_buffer_5
  assign buffer_2_out = {8{1'b0}};  // Buffer buffer_2, 8 bits wide
  Adder #(.width(16)) adder_1 (
    .a(controlled_inverter_1_out), .b(ALU_IN_A), .out(ALU_VALUE), .cin(SUB), .cout(CARR_BIT));
  assign BUS_1 = PRG_CNT_READ ? {buffer_2_out, counter_1_q} : 16'bz;  // Controlled_Buffer controlled_buffer_6
  // Probe on BUS_1
  Register #(.width(16)) DISP_REG (.D(BUS_1), .en(DISP_REG_WRITE), .clk(CLK), .Q(DISP_REG_q));  // open: clr
  Register #(.width(16)) B_REG (.D(BUS_1), .en(REG_B_WRITE), .clk(CLK), .Q(ALU_IN_B));  // open: clr
  assign BUS_1 = EO ? ALU_VALUE : 16'bz;  // Controlled_Buffer controlled_buffer_7
  // Probe on BUS_1
  // Probe on BUS_1
  // Probe on DISP_REG_q
  // Probe on DISP_REG_q
  not not_6 (not_6_out, REG_B_WRITE);
  Controlled_Buffer #(.width(8)) controlled_buffer_8 (.en(not_6_out));  // open: in, out
  // Probe on ALU_IN_B
  assign buffer_3_out = ALU_VALUE;  // Buffer buffer_3, 16 bits wide
  and and_3 (and_3_out[0], ~buffer_3_out[0], ~buffer_3_out[1], ~buffer_3_out[2], ~buffer_3_out[3], ~buffer_3_out[4], ~buffer_3_out[5], ~buffer_3_out[6], ~buffer_3_out[7], ~buffer_3_out[8], ~buffer_3_out[9], ~buffer_3_out[10], ~buffer_3_out[11], ~buffer_3_out[12], ~buffer_3_out[13], ~buffer_3_out[14], ~buffer_3_out[15]);  // AND_Gate
  // RGB_Video #(.height(64), .scale(4), .width(64)) rgb_video_1: pin names not known; wires that end beside it: CLK, DISP_REG_WRITE, rgb_video_1_p3, rgb_video_1_p4, DISP_REG_q[14:0]
  buf buffer_4 (and_3_out[2], 1'b0);
  buf buffer_5 (and_3_out[3], 1'b0);
  buf buffer_6 (and_3_out[4], 1'b0);
  buf buffer_7 (and_3_out[5], 1'b0);
  Register register_1 (
    .D({and_3_out[7:2], CARR_BIT, and_3_out[0]}), .en(FLAG_REG_WRITE), .clk(CLK),
    .Q({register_1_q, CARRY_FLAG, ZERO_FLAG}));  // open: clr
  buf buffer_8 (and_3_out[6], 1'b0);
  buf buffer_9 (and_3_out[7], 1'b0);
  // Shift_Register #(.length(2)) shift_register_1: pin names not known; wires that end beside it: 1'b1, DISP_REG_WRITE, DISP_REG_WRITE
  Register #(.width(16)) INSTR_REG (
    .D(BUS_1), .en(REG_INS_WRITE), .clk(CLK), .Q({INS_DECODER, INSTR_REG_q}));  // open: clr
  // Probe on INSTR_REG_q
  // Probe on {INS_DECODER, INSTR_REG_q}
  D_Flip_Flop d_ff_1 (.D(DISP_REG_WRITE), .clk(INV_CLK), .Q(d_ff_1_q));  // open: Qn, preset, reset
  not not_7 (not_7_out, REG_INS_WRITE);
  and and_4 (and_4_out, not_7_out, REG_INS_READ);
  assign buffer_10_out = 4'b0000;  // Buffer buffer_10, 4 bits wide
  // Probe on INS_DECODER
  Counter #(.max('h3f), .width(6)) counter_2 (
    .clk(d_ff_1_q), .carry(counter_2_carry), .Q(rgb_video_1_p3));  // open: clr, load, up, count, D
  assign BUS_1 = and_4_out ? {buffer_10_out, INSTR_REG_q} : 16'bz;  // Controlled_Buffer controlled_buffer_9
  Counter #(.max('h3f), .width(6)) counter_3 (
    .clk(and_5_out), .Q(rgb_video_1_p4));  // open: clr, load, up, count, D, carry
  buf and_5 (and_5_out, ~counter_2_carry);  // AND_Gate AND_Gate
  Counter #(.max('hfff), .width(12)) counter_4 (
    .clk(ROM_LOAD_CLOCK), .Q(counter_4_q));  // open: clr, load, up, count, D, carry
  Counter #(.max('h9), .width(4)) INSTR_STEP_COUNTER (
    .clr(EI), .clk(INV_CLK), .Q(INSTR_STEP_COUNTER_q));  // open: load, up, count, D, carry
  Register #(.width(16)) MEM_ADDRESS_REG (
    .D(BUS_1), .en(REG_MEMADDR_WRITE), .clk(CLK), .Q(MEM_ADDRESS_REG_q));  // open: clr
  // Probe on MEM_ADDRESS_REG_q[11:0]
  // Probe on MEM_ADDRESS_REG_q
  ROM #(.addrWidth(12), .dataWidth(16)) PROGRAM_ROM (.addr(counter_4_q), .data(PROGRAM_ROM_data));
  and and_6 (and_6_out, counter_4_q[0], counter_4_q[1], counter_4_q[2], counter_4_q[3], counter_4_q[4], counter_4_q[5], counter_4_q[6], counter_4_q[7], counter_4_q[8], counter_4_q[9], counter_4_q[10], counter_4_q[11]);
  Decoder #(.enable("false"), .select(4)) decoder_1 (.sel(INSTR_STEP_COUNTER_q));  // open: out0, out1, out2, out3, out4, out5, out6, out7, out8, out9, out10, out11, out12, out13, out14, out15
  DipSwitch #(.number(10)) dipswitch_2 (
    .sw1(dipswitch_2_sw10[9]), .sw2(dipswitch_2_sw10[8]), .sw3(dipswitch_2_sw10[7]),
    .sw4(dipswitch_2_sw10[6]), .sw5(dipswitch_2_sw10[5]), .sw6(dipswitch_2_sw10[4]),
    .sw7(dipswitch_2_sw10[3]), .sw8(dipswitch_2_sw10[2]), .sw9(dipswitch_2_sw10[1]),
    .sw10(dipswitch_2_sw10[0]));
  not not_8 (not_8_out, LOAD_ROM);
  assign controlled_buffer_10_out = not_8_out ? MEM_ADDRESS_REG_q[11:0] : 12'bz;  // Controlled_Buffer controlled_buffer_10
  assign controlled_buffer_10_out = LOAD_ROM ? counter_4_q : 12'bz;  // Controlled_Buffer controlled_buffer_11
  assign controlled_buffer_12_out = not_8_out ? MEM_WRITE : 1'bz;  // Controlled_Buffer controlled_buffer_12
  assign controlled_buffer_13_out = LOAD_ROM ? ROM_LOAD_CLOCK : 1'bz;  // Controlled_Buffer controlled_buffer_13
  assign controlled_buffer_13_out = not_8_out ? CLK : 1'bz;  // Controlled_Buffer controlled_buffer_14
  not not_9 (LOAD_ROM, and_6_out);
  assign controlled_buffer_15_out = 1'b1 ? INSTR_STEP_COUNTER_q : 4'bz;  // Controlled_Buffer controlled_buffer_15
  assign controlled_buffer_16_out = 1'b1 ? {ZERO_FLAG, CARRY_FLAG} : 2'bz;  // Controlled_Buffer controlled_buffer_16
  assign controlled_buffer_17_out = 1'b1 ? INS_DECODER : 4'bz;  // Controlled_Buffer controlled_buffer_17
  not not_10 (not_10_out, 1'b1);
  assign controlled_buffer_12_out = LOAD_ROM ? LOAD_ROM : 1'bz;  // Controlled_Buffer controlled_buffer_18
  assign controlled_buffer_19_out = not_11_out ? BUS_1 : 16'bz;  // Controlled_Buffer controlled_buffer_19
  assign controlled_buffer_19_out = LOAD_ROM ? PROGRAM_ROM_data : 16'bz;  // Controlled_Buffer controlled_buffer_20
  not not_11 (not_11_out, LOAD_ROM);
  // Probe on {controlled_buffer_17_out, controlled_buffer_15_out, controlled_buffer_16_out}
  ROM #(.addrWidth(10), .dataWidth(17)) rom_1 (
    .addr({controlled_buffer_17_out, controlled_buffer_15_out, controlled_buffer_16_out}),
    .data({SUB, REG_INS_WRITE, DISP_REG_WRITE, STOP, COUNT_ENABLE, PRG_CNT_READ, MEM_WRITE, REG_A_READ, EO, FLAG_REG_WRITE, JUMP, REG_B_WRITE, REG_A_WRITE, MEM_READ, REG_MEMADDR_WRITE, REG_INS_READ, EI}));
  assign {controlled_buffer_17_out, controlled_buffer_15_out, controlled_buffer_16_out} = not_10_out ? dipswitch_2_sw10 : 10'bz;  // Controlled_Buffer controlled_buffer_21
  RAM #(.addrWidth(12), .asyncread("true"), .dataWidth(16), .\type ("nonvolatile")) MEMORY (
    .addr(controlled_buffer_10_out), .we(controlled_buffer_12_out), .clk(controlled_buffer_13_out),
    .din(controlled_buffer_19_out), .dout(MEMORY_dout));  // open: oe
  not not_12 (not_12_out, EI);
  Controlled_Buffer #(.width(17)) controlled_buffer_22 (.en(not_12_out));  // open: in, out
  assign BUS_1 = MEM_READ ? MEMORY_dout : 16'bz;  // Controlled_Buffer controlled_buffer_23
  // Probe on MEMORY_dout

  // Notes on the sheet:
  //   BUS VALUE
  //   DISPLAY / OUTPUT
  //   contents of PROGRAM_ROM (hex, n*v repeats v):
  //   8000 7193 8001 7192 112a 7190 8002 7191 8001 3193 7193 1190 4191 7190 a008 1193 4192 7120 8000 7193
  //   8001 112b 7190 8002 7191 8001 3193 7193 1190 4191 7190 a019 1193 4192 7121 1120 7190 102d 7191 8000
  //   7193 1190 43e8 7190 a031 1193 712c 5000 6035 1193 3191 7193 6029 112a 33e8 712a 803f 412a a000 8000
  //   712a 112b 33e8 712b 803f 412b a000 8000 712b 6000 930*0 1
  //   contents of rom_1 (hex, n*v repeats v):
  //   4*804 4*9008 4*1 52*0 4*804 4*9008 4*6 4*18 4*1 44*0 4*804 4*9008 4*6 4*28 4*1 44*0 4*804 4*9008 4*6
  //   4*28 4*190 4*1 40*0 4*804 4*9008 4*6 4*28 4*10190 4*1 40*0 4*804 4*9008 4*4200 4*1 48*0 4*804 4*9008
  //   4*42 4*1 48*0 4*804 4*9008 4*6 4*600 4*1 44*0 4*804 4*9008 4*12 4*1 48*0 4*804 4*9008 1 1 42 42 4*1
  //   48*0 4*804 4*9008 1 42 1 42 4*1 48*0 4*804 4*9008 4*2000 4*1 48*0 4*804 4*9008 4*204 4*18 4*1
endmodule
